# Fritzing sketch diagrama carrito (saved by Fritzing 0.8.5b)
circuit board: 16.9333cm x 5.64444cm
breadboards: 1

parts:
  M1 = DC Motor
  M2 = DC Motor
  IC1 = L293D [package=THT]
  VCC1 = Battery block 9V
  Arduino1 = Arduino Uno (Rev3)
  VCC2 = 4 x AAA Battery Mount
  IR1 = TSOP312.., 314.. [package=THT]

nets:
  N1: M1.pin_1, IC1.Out_4_(_Controlled_by_Enable_2_)
  N2: M1.pin_2, IC1.Out_3_(_Controlled_by_Enable_2_)
  N3: M2.pin_1, IC1.Out_2_(_Controlled_by_Enable_1_)
  N4: M2.pin_2, IC1.Out_1_(_Controlled_by_Enable_1_)
  N5: IC1.Enable_1, Arduino1.D10_PWM/SS
  N6: IC1.In_1, Arduino1.D9_PWM
  GND: IC1.0V, VCC1.-, Arduino1.GND, IR1.GND
  N7: IC1.In_2, Arduino1.D8
  N8: IC1.+Vmotor, VCC1.+, Arduino1.VIN, VCC2.-
  N9: IC1.Enable_2, Arduino1.D11_PWM/MOSI
  N10: IC1.In_3, Arduino1.D13/SCK
  N11: IC1.In_4, Arduino1.D12/MISO
  N12: IC1.+V, VCC2.+, IR1.Vs
  N13: Arduino1.D7, IR1.Data
